# Fritzing sketch PIR-doorbell-indoor (saved by Fritzing 0.9.2b)
breadboards: 1

parts:
  Part2 = Arduino Ethernet Shield (Rev3)
  U1 = XBEE-1 [package=xbee-1]
  S1 = Pushbutton [package="[THT]"]
  R1 = Resistor [tolerance=±5% resistance=220 package=THT]

nets:
  GND: Part2.GND, U1.GND, R1.Pin_0
  N1: Part2.RX/D0, U1.DOUT
  N2: Part2.TX/D1, U1.DIN
  N3: Part2.D7, S1.Pin_1, S1.Pin_2, R1.Pin_1
  3V3: Part2.3V3, U1.VDD, S1.Pin_3, S1.Pin_4
