# Fritzing sketch PIR-doorbell-outdoor (saved by Fritzing 0.9.2b)
breadboards: 1

parts:
  Part1 = Arduino Uno (Rev3)
  U1 = XBee
  PIR1 = PIR sensor

nets:
  N1: Part1.A0, PIR1.SIG
  N2: Part1.D0/RX, U1.pin3
  N3: Part1.D1/TX, U1.pin2
  3V3: Part1.3V3, U1.VCC
  5V: Part1.5V, PIR1.VDD
  GND: Part1.GND, U1.GND, PIR1.GND
